# Fritzing sketch gloveSchematic (saved by Fritzing 0.9.9b)
breadboards: 1

parts:
  Part1 = Arduino Uno (Rev3)
  Part2 = Bluetooth HC-05 Macho
  Part3 = Triple Axis Accelerometer Breakout - ADXL335
  J1 = Piezo Speaker
  Part4 = Adafruit DRV2605L [part_number="Adafruit #2305"]
  U4 = Vibration Motor- ROB-08449 [package=vibe-motor-10mm]
  U5 = 7-SEGMENT-DISPLAY [package=7-segment-display]
  R1 = Resistor [tolerance=±5% resistance=220 package="1206 [SMD]"]
  R2 = Resistor [tolerance=±5% resistance=220 package="1206 [SMD]"]
  R3 = Resistor [tolerance=±5% resistance=220 package="1206 [SMD]"]
  R4 = Resistor [tolerance=±5% resistance=220 package="1206 [SMD]"]
  R5 = Resistor [tolerance=±5% resistance=220 package="1206 [SMD]"]
  R6 = Resistor [tolerance=±5% resistance=220 package="1206 [SMD]"]
  R7 = Resistor [tolerance=±5% resistance=220 package="1206 [SMD]"]
  R8 = Resistor [tolerance=±5% resistance=220 package="1206 [SMD]"]

nets:
  N1: Part1.A0, Part3.XOUT
  N2: Part1.A1, Part3.YOUT
  N3: Part1.A2, Part3.ZOUT
  N4: Part1.A4/SDA, Part4.SDA
  N5: Part1.A5/SCL, Part4.SCL
  N6: Part1.D8, R3.Pin_1
  N7: Part1.D9_PWM, R4.Pin_1
  N8: Part1.D10_PWM/SS, R7.Pin_1
  N9: Part1.D11_PWM/MOSI, R8.Pin_1
  N10: Part1.D12/MISO, Part2.RXD
  N11: Part1.D13/SCK, Part2.TXD
  N12: Part1.AREF, Part3.ST
  N13: Part1.D3_PWM, J1.pin2
  N14: Part1.D4, R2.Pin_0
  N15: Part1.D5_PWM, R1.Pin_0
  N16: Part1.D6_PWM, R6.Pin_0
  N17: Part1.D7, R5.Pin_0
  VCC: Part1.5V, Part2.VCC, Part3.VCC, Part4.VIN
  GND: Part1.GND, Part2.GND, Part3.GND, J1.pin1, Part4.GND, U5.F
  N18: Part4.OUT+, Part4.OUT-, U4.+, U4.-
  N19: U5.E, R2.Pin_1
  N20: U5.D, R6.Pin_1
  N21: U5.G1, R5.Pin_1
  N22: U5.DP, R7.Pin_0
  N23: U5.B, R8.Pin_0
  N24: U5.A, R4.Pin_0
  N25: U5.G2, R3.Pin_0
  N26: U5.G, R1.Pin_1

custom parts:
  Adafruit DRV2605L: The DRV2605 from TI is a fancy little motor driver. Rather than controlling a stepper motor or DC motor, its designed specifically for controlling haptic motors - buzzers and vibration motors. Normally one would just turn those kinds of motors on and off, but this driver has the ability to have various effects when driving a vibe motor. For example, ramping the vibration level up and down,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
